// Logisim project battleship.circ as structural Verilog: 2 circuits, main circuit main
module main (
  input  [3:0] PosicaoTiro,
  input  [3:0] Navio1,
  input  [3:0] Navio2,
  output Acertou,
  output Errou
);

  wire button_1_out, comparator_1_eq, comparator_2_eq, or_1_out;
  wire [3:0] undriven, undriven_2, undriven_3;

  Encoder encoder_1 (.in_1(undriven_3));
  Encoder encoder_2 (.in_1(undriven_2));
  Encoder encoder_3 (.in_1(undriven));
  Comparator #(.width(4)) comparator_1 (.a(undriven_2), .b(undriven_3), .eq(comparator_1_eq));  // open: gt, lt
  Comparator #(.width(4)) comparator_2 (.a(undriven_3), .b(undriven), .eq(comparator_2_eq));  // open: gt, lt
  Button button_1 (.out(button_1_out));
  or or_1 (or_1_out, comparator_1_eq, comparator_2_eq);
  and and_1 (Acertou, or_1_out, button_1_out);
  and and_2 (Errou, button_1_out, ~or_1_out);  // AND_Gate
endmodule

module Encoder (
  input  [3:0] in_1
);

  wire and_1_out, and_2_out, and_3_out, and_4_out, and_5_out, and_6_out, and_7_out, and_8_out, and_9_out,
       and_10_out, and_11_out, and_12_out;

  and and_1 (and_1_out, ~in_1[3], ~in_1[2], in_1[0]);  // AND_Gate
  and and_2 (and_2_out, ~in_1[3], in_1[2]);  // AND_Gate
  and and_3 (and_3_out, in_1[3], ~in_1[1], in_1[0]);  // AND_Gate
  and and_4 (and_4_out, in_1[3], in_1[1], ~in_1[0]);  // AND_Gate
  and and_5 (and_5_out, ~in_1[3], ~in_1[2], ~in_1[0]);  // AND_Gate
  and and_6 (and_6_out, ~in_1[3], in_1[1], in_1[0]);  // AND_Gate
  and and_7 (and_7_out, ~in_1[3], in_1[2], ~in_1[1]);  // AND_Gate
  and and_8 (and_8_out, in_1[3], in_1[1], ~in_1[0]);  // AND_Gate
  and and_9 (and_9_out, ~in_1[3], in_1[0]);  // AND_Gate
  and and_10 (and_10_out, in_1[1], in_1[0]);
  and and_11 (and_11_out, in_1[2], in_1[0]);
  and and_12 (and_12_out, ~in_1[3], in_1[2], ~in_1[1]);  // AND_Gate
  // OR_Gate or_1 has open pins: in0=and_1_out, in1=and_2_out, in2=and_3_out, in3=and_4_out, out=open
  // OR_Gate or_2 has open pins: in0=and_5_out, in1=and_6_out, in2=and_7_out, in3=and_8_out, out=open
  // OR_Gate or_3 has open pins: in0=and_9_out, in1=and_10_out, in2=and_11_out, in3=and_12_out, out=open
endmodule
